# Fritzing sketch esquematico (saved by Fritzing 0.9.2b)
breadboards: 1

parts:
  Raspberry_Pi1 = Raspberry Pi B+
  U2 = HC-SR04 [chip_label=IC package="SIP (Single Inline) [THT]"]
  R2 = Resistor [tolerance=±5% resistance=1k package=THT]
  R3 = Resistor [tolerance=±5% resistance=2.2k package=THT]

nets:
  N1: Raspberry_Pi1.GND, Raspberry_Pi1.GPIO24, Raspberry_Pi1.GPIO23, U2.Trig, R2.Pin_1, R3.Pin_1
  5V: Raspberry_Pi1.5V, U2.Vcc
  N2: U2.Echo, U2.GND, R2.Pin_0, R3.Pin_0

notes:
  1KΩ
  2KΩ
  VCC
  GPIO 23
  GPIO 24
  GND

custom parts:
  HC-SR04: HC-SR04 ultrasound distance sensor
